# Fritzing sketch stranger-lights (saved by Fritzing 0.9.2b)
breadboards: 1

parts:
  Part1 = FTDI Basic Programmer
  U1 = ATmega328 [package=dip]
  U2 = AVR 10-pin ICSP Header [package=avr_icsp]
  C1 = Ceramic Capacitor [capacitance=100nF package="100 mil [THT, multilayer]"]
  JP1 = Header 3 [package=screwterminal-3.5mm-3_lock.007s]

nets:
  N1: Part1.RXI, U1.PD1_(TXD)
  N2: Part1.TXO, U1.PD0_(RXD)
  N3: Part1.GND, U1.GND#7, U2.4, C1.1, JP1.1
  N4: U1.PC6_(RESET), U2.5
  N5: U1.VCC, U2.2, C1.0
  N6: U1.PB1, JP1.2
  N7: U1.PB3_(MOSI), U2.1
  N8: U1.PB4_(MISO), U2.9
  N9: U1.PB5_(SCK), U2.7

notes:
  Flash Programmer
  +12 V
  LED Strip

custom parts:
  ATmega328: Atmel ATmega328 microcontroller.
